# Fritzing sketch schema_serre (saved by Fritzing 0.9.3b)
circuit board: 7.10536cm x 5.46426cm
breadboards: 1

parts:
  Composant1 = Arduino Uno (Rev3)
  Q1 = Basic FET P-Channel [package="TO220 [THT]"]
  RHT1 = Humidity and Temperature Sensor RHT03
  LightSensor = screw terminal, 3 pins
  SerialConnector = female pin header, 4 pins [form="♀ (female)"]
  J4 = Screw terminal - 2 pins [package=THT]
  J5 = Screw terminal - 2 pins [package=THT]
  MoistureSensor = screw terminal, 3 pins
  R1 = Resistor [tolerance=±5% resistance=10k package=THT]
  R2 = Resistor [tolerance=±5% resistance=10k package=THT]
  J7 = Screw terminal - 2 pins [package=THT]
  Q2 = Basic FET P-Channel [package="TO220 [THT]"]
  U1 = Voltage Regulator - 5V [package="DPak [SMD]"]

nets:
  N1: Composant1.A0, MoistureSensor.pin2
  N2: Composant1.A1, LightSensor.pin2
  GND: Composant1.GND, Q1.source, RHT1.GND_2, LightSensor.pin1, SerialConnector.pin4, MoistureSensor.pin1, R1.Pin_1, R2.Pin_1, J7.pin1, Q2.source, U1.GND
  N3: Composant1.D0/RX, SerialConnector.pin3
  N4: Composant1.D1/TX, SerialConnector.pin2
  N5: Composant1.D2, RHT1.Data-signal
  N6: Composant1.D3_PWM, Q1.gate, R1.Pin_0
  N7: Composant1.D5_PWM, R2.Pin_0, Q2.gate
  12V: Composant1.VIN, J4.pin1, J5.pin1, J7.pin2, U1.input_voltage
  N8: Q1.drain, J4.pin2
  5V: RHT1.Vcc, LightSensor.pin3, SerialConnector.pin1, MoistureSensor.pin3, U1.output_voltage
  N9: J5.pin2, Q2.drain

notes:
  Moisture Sensor
  Pump Actuator
  Light Control
  Light Sensor
  Serial Communication
  Power 12v
